# Fritzing sketch Sistemas de riego (saved by Fritzing 0.9.3b)
breadboards: 2

parts:
  Componente1 = Arduino Uno (Rev3)
  RHT1 = Humidity and Temperature Sensor RHT03  # not connected
  R1 = PHOTOCELL [package=photocell]
  J1 = Basic Servo
  Componente2 = Soil Moisture Sensor
  D_O_Circuit1 = D.O. Circuit
  Componente3 = Soil Moisture Sensor
  Componente4 = Soil Moisture Sensor
  R2 = Resistor [tolerance=±5% resistance=220 package="2512 [SMD]"]
  LED1 = RGB LED (com. cathode, rgb) [package="5 mm [THT]"]
  R3 = Resistor [tolerance=±5% resistance=220 package=THT]
  R4 = Resistor [tolerance=±5% resistance=220 package=THT]
  R5 = Resistor [tolerance=±5% resistance=220 package=THT]

nets:
  N1: Componente1.A0, D_O_Circuit1.GND
  N2: Componente1.A1, R1.P$2, R2.Pin_0
  N3: Componente1.A2, Componente2.SIG
  N4: Componente1.A3, Componente4.SIG
  N5: Componente1.A4/SDA, Componente3.SIG
  N6: Componente1.D9_PWM, J1.pulse
  GND: Componente1.GND, R1.P$1, J1.gnd, Componente2.GND, D_O_Circuit1.RX, Componente3.GND, LED1.common_cathode
  N7: Componente1.D3_PWM, R3.Pin_1
  N8: Componente1.D4, R4.Pin_1
  N9: Componente1.D5_PWM, R5.Pin_1
  VCC: Componente1.5V, J1.vcc, Componente2.VCC, D_O_Circuit1.TX, Componente3.VCC, Componente4.VCC, R2.Pin_1
  N10: LED1.red_anode, R3.Pin_0
  N11: LED1.green_anode, R4.Pin_0
  N12: LED1.blue_anode, R5.Pin_0

// code stored in the sketch: SistemaDeriegoFriz.ino
#include <SimpleDHT.h>
#include <Servo.h>

//----------------------------------- Asociacion las salidas correspondiente.
// Analogicas
#define MEDIDOR_NIVEL_AGUA A0
#define FOTOCELDA A1
#define SENSOR_SUELO_1 A2
#define SENSOR_SUELO_2 A3
#define SENSOR_SUELO_3 A4

//Digitales
#define MEDIDOR_hUMEDAD_TEMP 2
#define LED_ROJO 3
#define LED_VERDE 4
#define LED_AZUL 5
#define SERVO 9

//Variables
int NIVEL_AGUA = 0;           //SENSOR NIVELAGUA
int NIVEL_ANTERIOR_AGUA = 0;  //SENSOR NIVELAGUA
char PRINTBUFFER[128];        //SENSOR NIVELAGUA

int VALOR_CLARIDAD = 0;       //SENSOR FOTOCELDA    

int HUMEDADA_TEMP;            //SENSOR HUMEDAD SUELO 
int HUMEDADA_FINAL_1;         //SENSOR HUMEDAD SUELO
int HUMEDADA_FINAL_2;         //SENSOR HUMEDAD SUELO 
int HUMEDADA_FINAL_3;         //SENSOR HUMEDAD SUELO

byte VALOR_HUMEDAD = 0;       //SENSOR HUMEDAD/TEMP
byte VALOR_TEMPERATURA = 0;   //SENSOR HUMEDAD/TEMP

#define delayTime 10 //LEDS

int POSICION = 0;             // SERVO 
int IPOSICIONACTUAL = 1;      // SERVO 

// Crear Obj
SimpleDHT11 DHT11;
Servo MYSERVO;  

void setup(){
  Serial.begin(9600);
  
  pinMode(FOTOCELDA,INPUT); 
  MYSERVO.attach(SERVO); 

  pinMode(LED_ROJO, OUTPUT);
  pinMode(LED_VERDE, OUTPUT);
  pinMode(LED_AZUL, OUTPUT);
  
  // Valores iniciales led
  digitalWrite(LED_ROJO, HIGH);
  digitalWrite(LED_VERDE, LOW);
  digitalWrite(LED_AZUL, LOW);
}

void loop(){
  delay(1000);
  obtenerOtros();
  obtenerValoresPlantas();
 delay(1000);
 //mover_Servo(1);
 //delay(1000);
 //mover_Servo(2);
 //delay(1000);
 //mover_Servo(3);
}

void obtenerOtros(){
  obtener_Nivel_Del_Agua();
  obtener_Humedad_Temperatura();
  obtener_Claridad();
}

void obtenerValoresPlantas(){
 obtenerHumedadSuelo(1);
 obtenerHumedadSuelo(2);
 obtenerHumedadSuelo(3);
}

void obtener_Nivel_Del_Agua (){
    NIVEL_AGUA = analogRead(MEDIDOR_NIVEL_AGUA);

    if(((NIVEL_ANTERIOR_AGUA>=NIVEL_AGUA) && ((NIVEL_ANTERIOR_AGUA - NIVEL_AGUA) > 10)) || ((NIVEL_ANTERIOR_AGUA<NIVEL_AGUA) && ((NIVEL_AGUA - NIVEL_ANTERIOR_AGUA) > 10)))
    {
      sprintf(PRINTBUFFER,"ADC%d level is %d\n",MEDIDOR_NIVEL_AGUA, NIVEL_AGUA);
      Serial.print(PRINTBUFFER);
      NIVEL_ANTERIOR_AGUA = NIVEL_AGUA;
    }  
}

void obtener_Humedad_Temperatura () {
  byte DATA[40] = {0};
  if (DHT11.read(MEDIDOR_hUMEDAD_TEMP, &VALOR_TEMPERATURA, &VALOR_HUMEDAD, DATA)) {
    Serial.print("Lectura erronea sensor Humedad/Temperatura");
    return;
  }
  Serial.print((int)VALOR_HUMEDAD); Serial.println(" % HUMEDAD AMBIENTAL");
  Serial.print((int)VALOR_TEMPERATURA); Serial.print(" *C TEMPERATURA AMBIENTAL");
}

void obtener_Claridad (){
  VALOR_CLARIDAD = analogRead(FOTOCELDA);
  Serial.println(VALOR_CLARIDAD); Serial.println(" % CLARIDAD");
}

void mover_Servo(int IPLANTA) {
  if (IPLANTA == 1) {
    MYSERVO.write(0); 
  } else if (IPLANTA == 2) {
    MYSERVO.write(90); 
  } else if (IPLANTA == 3) {
    MYSERVO.write(180); 
  } 
}

void obtenerHumedadSuelo(int IPLANTA) {

    if (IPLANTA == 1) {
      HUMEDADA_FINAL_1 = 0;         
      HUMEDADA_TEMP = map(analogRead(SENSOR_SUELO_1), 0, 1023, 100, 0);
      HUMEDADA_FINAL_1 = constrain (HUMEDADA_TEMP, 0, 100);
      Serial.print(HUMEDADA_FINAL_1); Serial.println("% de humedad Planta 1");
      if ((HUMEDADA_FINAL_1 >= 0) and (HUMEDADA_FINAL_1 <= 33)) {
        Serial.println("Suelo seco Planta 1");
      } else if ((HUMEDADA_FINAL_1 >= 34) and (HUMEDADA_FINAL_1 <= 66)) {
        Serial.println("Suelo humedo Planta 1");
      } else {
        Serial.println("Suelo mojado Planta 1");
      }
    } else if (IPLANTA == 2) {
      HUMEDADA_FINAL_2 = 0; 
      HUMEDADA_TEMP = map(analogRead(SENSOR_SUELO_2), 0, 1023, 100, 0);
      HUMEDADA_FINAL_2 = constrain (HUMEDADA_TEMP, 0, 100);
      Serial.print(HUMEDADA_FINAL_2); Serial.println("% de humedad Planta 2");
      if ((HUMEDADA_FINAL_2 >= 0) and (HUMEDADA_FINAL_2 <= 33)) {
        Serial.println("Suelo seco Planta 2");
      } else if ((HUMEDADA_FINAL_2 >= 34) and (HUMEDADA_FINAL_2 <= 66)) {
        Serial.println("Suelo humedo Planta 2");
      } else {
        Serial.println("Suelo mojado Planta 2");
      }
    } else if (IPLANTA == 3) {
      HUMEDADA_FINAL_3 = 0; 
      HUMEDADA_TEMP = map(analogRead(SENSOR_SUELO_3), 0, 1023, 100, 0);
      HUMEDADA_FINAL_3 = constrain (HUMEDADA_TEMP, 0, 100);   
      Serial.print(HUMEDADA_FINAL_3); Serial.println("% de humedad Planta 3");
      if ((HUMEDADA_FINAL_3 >= 0) and (HUMEDADA_FINAL_3 <= 33)) {
        Serial.println("Suelo seco Planta 3");
      } else if ((HUMEDADA_FINAL_3 >= 34) and (HUMEDADA_FINAL_3 <= 66)) {
        Serial.println("Suelo humedo Planta 3");
      } else {
        Serial.println("Suelo mojado Planta 3");
      }
    }
}

void cambiarColorLed(String SCOLOR) {
  if (SCOLOR == "ROJO") {
    digitalWrite(LED_ROJO, HIGH);
    digitalWrite(LED_VERDE, LOW);
    digitalWrite(LED_AZUL, LOW); 
  } else if (SCOLOR == "VERDE") {
    digitalWrite(LED_ROJO, LOW);
    digitalWrite(LED_VERDE, HIGH);
    digitalWrite(LED_AZUL, LOW);
  } else if (SCOLOR == "AZUL") {
    digitalWrite(LED_ROJO, LOW);
    digitalWrite(LED_VERDE, LOW);
    digitalWrite(LED_AZUL, HIGH); 
  } else if (SCOLOR == "BLANCO") {
    digitalWrite(LED_ROJO, LOW);
    digitalWrite(LED_VERDE, LOW);
    digitalWrite(LED_AZUL, LOW); 
  } 
}
